// Logisim project cpu.circ as structural Verilog: 5 circuits, main circuit main
module main (
  input  [31:0] INSTRUCTION,
  input  CLOCK,
  output [31:0] PROGRAM_COUNTER,
  output [31:0] ra,
  output [31:0] sp,
  output [31:0] t0,
  output [31:0] t1,
  output [31:0] t2,
  output [31:0] s0,
  output [31:0] s1,
  output [31:0] a0
);

  wire DMEM_p1, DMEM_p6, DMEM_p8;
  wire [31:0] alu, DMEM_p9, immediate_generator_1_immout, multiplexer_1_out, multiplexer_2_out,
       multiplexer_3_out, multiplexer_4_out, pc_plus_4, RegFile_read_data_1, RegFile_read_data_2,
       register_1_q;

  Adder #(.width(32)) adder_1 (.a(PROGRAM_COUNTER), .b(32'h4), .out(pc_plus_4));  // open: cin, cout
  Multiplexer #(.width(32), .enable("false")) multiplexer_1 (
    .in0(pc_plus_4), .in1(alu), .out(multiplexer_1_out));  // open: sel
  Register #(.width(32)) PC (.D(multiplexer_1_out), .clk(CLOCK), .Q(PROGRAM_COUNTER));  // open: en, clr
  Register #(.width(32)) register_1 (.D(INSTRUCTION), .en(1'b0), .clk(CLOCK), .Q(register_1_q));  // open: clr
  immediate_generator immediate_generator_1 (
    .imm(register_1_q[31:7]), .immOut(immediate_generator_1_immout));  // open: ImmSel
  regfile_main RegFile (
    .rs2(register_1_q[24:20]), .rd(register_1_q[11:7]), .Read_Data_1(RegFile_read_data_1),
    .Read_Data_2(RegFile_read_data_2), .ra(ra), .sp(sp), .t0(t0), .t1(t1), .t2(t2), .s0(s0), .s1(s1),
    .a0(a0), .rs1(register_1_q[19:15]), .Write_Data(multiplexer_4_out), .clk(CLOCK));  // open: RegWEn
  Multiplexer #(.width(32), .enable("false")) multiplexer_2 (
    .in0(RegFile_read_data_1), .in1(PROGRAM_COUNTER), .out(multiplexer_2_out));  // open: sel
  Multiplexer #(.width(32), .enable("false")) multiplexer_3 (
    .in0(RegFile_read_data_2), .in1(immediate_generator_1_immout), .out(multiplexer_3_out));  // open: sel
  alu Arithmetic_Logic_Unit (.B(multiplexer_3_out), .Result(alu), .A(multiplexer_2_out));  // open: ALUSel
  // mem_main DMEM: pin names not known; wires that end beside it: DMEM_p1, alu, RegFile_read_data_2, DMEM_p1, CLOCK, DMEM_p6, DMEM_p6, DMEM_p8, DMEM_p9
  Multiplexer #(.select(2), .width(32), .enable("false")) multiplexer_4 (
    .in0(pc_plus_4), .in1(alu), .in2(DMEM_p9), .out(multiplexer_4_out));  // open: in3, sel

  // Other names for the same wires on the sheet: clk = CLOCK

  // Notes on the sheet:
  //   Output
  //   IMEM (do **NOT** move this)
  //   Inputs
  //   Inputs/Outputs for testing. Do **NOT** move these.
endmodule

module control_module (
  input  BrEq,
  input  BrLt,
  input  [31:0] Instruction_32,
  output ASel,
  output [3:0] ALUSel,
  output BSel,
  output [1:0] WBSel,
  output MemRW,
  output BrUn,
  output RegWEn,
  output [2:0] ImmSel,
  output PCSel
);

  wire add, and_2_out, comparator_4_eq, comparator_5_eq, comparator_6_eq, comparator_7_eq, comparator_8_eq,
       comparator_9_eq, comparator_10_eq, comparator_11_eq, comparator_12_eq, comparator_13_eq,
       comparator_14_eq, comparator_15_eq, comparator_16_eq, comparator_17_eq, comparator_18_eq, isAdd,
       isMul, isSub, not_1_out, not_2_out, not_3_out, not_4_out, not_5_out, not_6_out, not_7_out, not_8_out,
       not_9_out, not_10_out, not_11_out, not_12_out, not_13_out;
  wire [16:0] instID;
  wire [31:0] undriven;

  not not_1 (not_1_out, undriven[31]);
  not not_2 (not_2_out, undriven[30]);
  not not_3 (not_3_out, undriven[29]);
  not not_4 (not_4_out, undriven[28]);
  not not_5 (not_5_out, undriven[27]);
  not not_6 (not_6_out, undriven[26]);
  not not_7 (not_7_out, undriven[25]);
  not not_8 (not_8_out, undriven[14]);
  not not_9 (not_9_out, undriven[13]);
  not not_10 (not_10_out, undriven[12]);
  not not_11 (not_11_out, undriven[6]);
  not not_12 (not_12_out, undriven[3]);
  not not_13 (not_13_out, undriven[2]);
  Comparator #(.width(17), .mode("unsigned")) comparator_1 (.a(instID), .b({17{1'b0}}), .eq(isAdd));  // open: gt, lt
  Comparator #(.width(17), .mode("unsigned")) comparator_2 (.a(instID), .b({17{1'b0}}), .eq(isMul));  // open: gt, lt
  Comparator #(.width(17), .mode("unsigned")) comparator_3 (.a(instID), .b({17{1'b0}}), .eq(isSub));  // open: gt, lt
  and and_1 (add, not_1_out, not_2_out, not_3_out, not_4_out, not_5_out, not_6_out, not_7_out, not_8_out, not_9_out, not_10_out, not_11_out, undriven[5], undriven[4], not_12_out, not_13_out, undriven[1], undriven[0]);
  type_determiner type_determiner_1 (.Opcode(Instruction_32[6:0]), .InstrType(ImmSel));
  Comparator #(.width(3), .mode("unsigned")) comparator_4 (
    .a(ImmSel), .b(3'b010), .eq(comparator_4_eq));  // open: gt, lt
  Comparator #(.width(3), .mode("unsigned")) comparator_5 (
    .a(Instruction_32[14:12]), .b(3'b000), .eq(comparator_5_eq));  // open: gt, lt
  Comparator #(.width(3), .mode("unsigned")) comparator_6 (
    .a(ImmSel), .b(3'b011), .eq(comparator_6_eq));  // open: gt, lt
  Comparator #(.width(3), .mode("unsigned")) comparator_7 (
    .a(Instruction_32[14:12]), .b(3'b010), .eq(comparator_7_eq));  // open: gt, lt
  Comparator #(.width(3), .mode("unsigned")) comparator_8 (
    .a(ImmSel), .b(3'b100), .eq(comparator_8_eq));  // open: gt, lt
  Comparator #(.width(3), .mode("unsigned")) comparator_9 (
    .a(Instruction_32[14:12]), .b(3'b110), .eq(comparator_9_eq));  // open: gt, lt
  Comparator #(.width(3), .mode("unsigned")) comparator_10 (
    .a(ImmSel), .b(3'b001), .eq(comparator_10_eq));  // open: gt, lt
  Comparator #(.width(3), .mode("unsigned")) comparator_11 (
    .a(ImmSel), .b(3'b010), .eq(comparator_11_eq));  // open: gt, lt
  Comparator #(.width(3), .mode("unsigned")) comparator_12 (
    .a(ImmSel), .b(3'b101), .eq(comparator_12_eq));  // open: gt, lt
  Comparator #(.width(3), .mode("unsigned")) comparator_13 (
    .a(ImmSel), .b(3'b110), .eq(comparator_13_eq));  // open: gt, lt
  Comparator #(.width(3), .mode("unsigned")) comparator_14 (
    .a(ImmSel), .b(3'b100), .eq(comparator_14_eq));  // open: gt, lt
  Comparator #(.width(3), .mode("unsigned")) comparator_15 (
    .a(ImmSel), .b(3'b110), .eq(comparator_15_eq));  // open: gt, lt
  and and_2 (and_2_out, comparator_4_eq, comparator_5_eq);
  Comparator #(.width(3), .mode("unsigned")) comparator_16 (
    .a(ImmSel), .b(3'b100), .eq(comparator_16_eq));  // open: gt, lt
  Comparator #(.width(3), .mode("unsigned")) comparator_17 (
    .a(ImmSel), .b(3'b110), .eq(comparator_17_eq));  // open: gt, lt
  or or_1 (ASel, comparator_16_eq, comparator_17_eq);
  Comparator #(.width(3), .mode("unsigned")) comparator_18 (
    .a(ImmSel), .b(3'b001), .eq(comparator_18_eq));  // open: gt, lt
  and and_3 (MemRW, comparator_6_eq, comparator_7_eq);
  and and_4 (BrUn, comparator_8_eq, comparator_9_eq);
  or or_2 (RegWEn, comparator_10_eq, comparator_11_eq, comparator_12_eq, comparator_13_eq);
  or or_3 (PCSel, comparator_14_eq, comparator_15_eq, and_2_out);
  not not_14 (BSel, comparator_18_eq);

  // Other names for the same wires on the sheet: inst_type[2:0] = ImmSel; instID_I_S_SB[2:0] = Instruction_32[14:12];
  //   instID_R[9:0] = {Instruction_32[31:25], Instruction_32[14:12]}; instID_U_UJ[6:0] = Instruction_32[6:0]

  // Notes on the sheet:
  //   Type Determiner
  //   R-func7func3
  //   opcode
  //   I/S/SB(B)-func3
  //   U/UJ(J)-opcode
  //   jalr
  //   sw
  //   bltu
endmodule

module immediate_generator (
  input  [2:0] ImmSel,
  input  [24:0] imm,
  output [31:0] immOut
);

  wire [31:0] i, s, sb, uj;

  assign i = {{20{imm[24]}}, imm[24:13]};  // Bit_Extender bit_extender_1
  assign s = {{20{imm[24]}}, {imm[24:18], imm[4:0]}};  // Bit_Extender bit_extender_2
  assign sb = {{19{imm[24]}}, {imm[24], imm[0], imm[23:18], imm[4:1], 1'b0}};  // Bit_Extender bit_extender_3
  assign uj = {{11{imm[24]}}, {imm[24], imm[12:5], imm[13], imm[23:14], 1'b0}};  // Bit_Extender bit_extender_4
  Multiplexer #(.select(3), .width(32), .enable("false")) multiplexer_1 (
    .in1({32{1'b1}}), .in2(i), .in3(s), .in4(sb), .in5({imm[24:5], {12{1'b0}}}), .in6(uj), .out(immOut),
    .sel(ImmSel));  // open: in0, in7

  // Other names for the same wires on the sheet: immIn[24:0] = imm; u[31:12] = imm[24:5]
endmodule

module type_determiner (
  input  [6:0] Opcode,
  output [2:0] InstrType
);

  wire comparator_1_eq, comparator_2_eq, comparator_3_eq, comparator_4_eq, comparator_5_eq, comparator_6_eq,
       comparator_7_eq, comparator_8_eq, or_1_out;
  wire [3:0] adder_1_out, adder_2_out, adder_3_out, adder_4_out, multiplexer_1_out, multiplexer_2_out,
       multiplexer_3_out, multiplexer_4_out, multiplexer_5_out, multiplexer_6_out;
  wire [3:3] adder_5_out;

  Comparator #(.width(7), .mode("unsigned")) comparator_1 (
    .a(Opcode), .b(7'b0110011), .eq(comparator_1_eq));  // open: gt, lt
  Comparator #(.width(7), .mode("unsigned")) comparator_2 (
    .a(Opcode), .b(7'b0000011), .eq(comparator_2_eq));  // open: gt, lt
  Comparator #(.width(7), .mode("unsigned")) comparator_3 (
    .a(Opcode), .b(7'b0010011), .eq(comparator_3_eq));  // open: gt, lt
  Comparator #(.width(7), .mode("unsigned")) comparator_4 (
    .a(Opcode), .b(7'b1100111), .eq(comparator_4_eq));  // open: gt, lt
  Comparator #(.width(7), .mode("unsigned")) comparator_5 (
    .a(Opcode), .b(7'b0100011), .eq(comparator_5_eq));  // open: gt, lt
  Comparator #(.width(7), .mode("unsigned")) comparator_6 (
    .a(Opcode), .b(7'b1100011), .eq(comparator_6_eq));  // open: gt, lt
  Comparator #(.width(7), .mode("unsigned")) comparator_7 (
    .a(Opcode), .b(7'b0110111), .eq(comparator_7_eq));  // open: gt, lt
  Comparator #(.width(7), .mode("unsigned")) comparator_8 (
    .a(Opcode), .b(7'b1101111), .eq(comparator_8_eq));  // open: gt, lt
  Multiplexer #(.width(4), .enable("false")) multiplexer_1 (
    .in0(4'b0000), .in1(4'b0001), .out(multiplexer_1_out), .sel(comparator_1_eq));
  or or_1 (or_1_out, comparator_2_eq, comparator_3_eq, comparator_4_eq);
  Multiplexer #(.width(4), .enable("false")) multiplexer_2 (
    .in0(4'b0000), .in1(4'b0011), .out(multiplexer_2_out), .sel(comparator_5_eq));
  Multiplexer #(.width(4), .enable("false")) multiplexer_3 (
    .in0(4'b0000), .in1(4'b0010), .out(multiplexer_3_out), .sel(or_1_out));
  Multiplexer #(.width(4), .enable("false")) multiplexer_4 (
    .in0(4'b0000), .in1(4'b0100), .out(multiplexer_4_out), .sel(comparator_6_eq));
  Multiplexer #(.width(4), .enable("false")) multiplexer_5 (
    .in0(4'b0000), .in1(4'b0101), .out(multiplexer_5_out), .sel(comparator_7_eq));
  Multiplexer #(.width(4), .enable("false")) multiplexer_6 (
    .in0(4'b0000), .in1(4'b0110), .out(multiplexer_6_out), .sel(comparator_8_eq));
  Adder #(.width(4)) adder_1 (.a(multiplexer_1_out), .b(multiplexer_3_out), .out(adder_1_out));  // open: cin, cout
  Adder #(.width(4)) adder_2 (.a(adder_1_out), .b(multiplexer_2_out), .out(adder_2_out));  // open: cin, cout
  Adder #(.width(4)) adder_3 (.a(adder_2_out), .b(multiplexer_4_out), .out(adder_3_out));  // open: cin, cout
  Adder #(.width(4)) adder_4 (.a(adder_3_out), .b(multiplexer_5_out), .out(adder_4_out));  // open: cin, cout
  Adder #(.width(4)) adder_5 (
    .a(adder_4_out), .b(multiplexer_6_out), .out({adder_5_out[3], InstrType}));  // open: cin, cout

  // Notes on the sheet:
  //   R
  //   I
  //   S
  //   SB
  //   U
  //   UJ
endmodule

module branch_comp (
  input  [31:0] rs1,
  input  [31:0] rs2,
  input  BrUn,
  output BrEq,
  output BrLT
);

  wire comparator_1_eq, comparator_2_eq, comparator_3_lt, comparator_4_lt;

  Comparator #(.width(32)) comparator_1 (.a(rs1), .b(rs2), .eq(comparator_1_eq));  // open: gt, lt
  Comparator #(.width(32), .mode("unsigned")) comparator_2 (.a(rs1), .b(rs2), .eq(comparator_2_eq));  // open: gt, lt
  Comparator #(.width(32)) comparator_3 (.a(rs1), .b(rs2), .lt(comparator_3_lt));  // open: gt, eq
  Comparator #(.width(32), .mode("unsigned")) comparator_4 (.a(rs1), .b(rs2), .lt(comparator_4_lt));  // open: gt, eq
  Multiplexer #(.enable("false")) multiplexer_1 (.in0(comparator_1_eq), .in1(comparator_2_eq), .out(BrEq), .sel(BrUn));
  Multiplexer #(.enable("false")) multiplexer_2 (.in0(comparator_3_lt), .in1(comparator_4_lt), .out(BrLT), .sel(BrUn));

  // Other names for the same wires on the sheet: A[31:0] = rs1; B[31:0] = rs2
endmodule
